# Fritzing sketch SmartCoffeeMachineSketch (saved by Fritzing 0.9.3b)
breadboards: 1

parts:
  Componente1 = Arduino Uno (Rev3)
  PIR1 = PIR_sensor
  Componente2 = SRF05 Ultrasonic Rangefinder
  U1 = POT [package=pot_alpha_rv16af-20]
  S1 = Momentary Switch [package=ksa_sealed_tac_switch]
  LED1 = smd LED [color="Red (633nm)" package="0603 [SMD]"]
  LED2 = smd LED [color="Red (633nm)" package="0603 [SMD]"]
  LED3 = smd LED [color="Red (633nm)" package="0603 [SMD]"]
  R1 = Resistor [tolerance=±5% resistance=220 package="2512 [SMD]"]
  R2 = Resistor [tolerance=±5% resistance=220 package="2512 [SMD]"]
  R3 = Resistor [tolerance=±5% resistance=220 package="2512 [SMD]"]
  R4 = Resistor [tolerance=±5% resistance=10 package=THT]

nets:
  N1: Componente1.A5/SCL, U1.S
  N2: Componente1.D8, Componente2.Echo
  N3: Componente1.D9_PWM, Componente2.Trig
  N4: Componente1.D2, PIR1.connector2
  N5: Componente1.D4, S1.1
  N6: Componente1.D5_PWM, R1.Pin_1
  N7: Componente1.D6_PWM, R2.Pin_1
  5V: Componente1.5V, PIR1.connector1, Componente2.VCC, U1.A, S1.4
  GND: Componente1.GND, PIR1.connector3, Componente2.GND, U1.E, LED1.cathode, LED2.cathode, LED3.cathode, R4.Pin_1
  N8: S1.2, R4.Pin_0
  N9: LED1.anode, R3.Pin_0
  N10: LED2.anode, R2.Pin_0
  N11: LED3.anode, R1.Pin_0
